// Logisim project 1686296849_BoothMultiplication.circ as structural Verilog: 3 circuits, main circuit main
module main (
  output [7:0] out_1,
  output [7:0] out_2
);

  wire and_1_out, clock_1_out, counter_1_carry, EAQ_Shifter_q__1_prime, n7_segment_decoder_1_a,
       n7_segment_decoder_1_b, n7_segment_decoder_1_c, n7_segment_decoder_1_d, n7_segment_decoder_1_e,
       n7_segment_decoder_1_f, n7_segment_decoder_1_g;
  wire [1:0] Q__1_q;
  wire [3:0] counter_1_q;
  wire [7:0] adder_1_out, adder_2_out, B_q, EAQ_Shifter_a_prime, EAQ_Shifter_q_prime, multiplexer_1_out,
       not_1_out;

  Clock clock_1 (.out(clock_1_out));
  Register B (.Q(B_q), .clk(and_1_out));  // open: D, en, clr
  assign not_1_out = ~B_q;  // NOT_Gate not_1, 8 bits wide
  and and_1 (and_1_out, clock_1_out, ~counter_1_carry);  // AND_Gate
  Multiplexer #(.select(2), .width(8), .enable("false")) multiplexer_1 (
    .in0({8{1'b0}}), .in1(B_q), .in2(adder_1_out), .in3({8{1'b0}}), .out(multiplexer_1_out), .sel(Q__1_q));
  Adder adder_1 (.a(not_1_out), .b(8'h1), .out(adder_1_out));  // open: cin, cout
  Register A (.D(EAQ_Shifter_a_prime), .Q(out_1), .clk(and_1_out));  // open: en, clr
  Adder adder_2 (.a(multiplexer_1_out), .b(out_1), .out(adder_2_out));  // open: cin, cout
  Register Q (.D(EAQ_Shifter_q_prime), .Q(out_2), .clk(and_1_out));  // open: en, clr
  Bit_Extender #(.out_width(1)) bit_extender_1 (.in(out_2), .out(Q__1_q[1]));
  D_Flip_Flop Q__1 (.clk(and_1_out), .D(EAQ_Shifter_q__1_prime), .Q(Q__1_q[0]));  // open: Qn, preset, en, reset
  EAQ_Shifter EAQ_Shifter (
    .Q__1(Q__1_q[0]), .A(adder_2_out), .Q(out_2), .Q__1_prime(EAQ_Shifter_q__1_prime),
    .A_prime(EAQ_Shifter_a_prime), .Q_prime(EAQ_Shifter_q_prime));
  Counter #(.width(4), .max('hf), .ongoal("stay"), .trigger("falling")) counter_1 (
    .load(1'b1), .Q(counter_1_q), .carry(counter_1_carry), .clk(clock_1_out));  // open: D, count, clr
  _7_Segment_Decoder u_7_segment_decoder_1 (
    .in_1(counter_1_q), .A(n7_segment_decoder_1_a), .B(n7_segment_decoder_1_b), .C(n7_segment_decoder_1_c),
    .D(n7_segment_decoder_1_d), .E(n7_segment_decoder_1_e), .F(n7_segment_decoder_1_f),
    .G(n7_segment_decoder_1_g));
  _7_Segment_Display u_7_segment_display_1 (
    .g(n7_segment_decoder_1_g), .f(n7_segment_decoder_1_f), .a(n7_segment_decoder_1_a),
    .b(n7_segment_decoder_1_b), .e(n7_segment_decoder_1_e), .d(n7_segment_decoder_1_d),
    .c(n7_segment_decoder_1_c));  // open: dp

  // Notes on the sheet:
  //   Final Answer
  //   SEQUENCE COUNTER
endmodule

module EAQ_Shifter (
  input  Q__1,
  input  [7:0] A,
  input  [7:0] Q,
  output Q__1_prime,
  output [7:0] A_prime,
  output [7:0] Q_prime
);

  Shifter #(.width(17), .shift("ar")) shifter_1 (
    .in({A, Q, Q__1}), .\dist (5'b00001), .out({A_prime, Q_prime, Q__1_prime}));
endmodule

module _7_Segment_Decoder (
  input  [3:0] in_1,
  output A,
  output B,
  output C,
  output D,
  output E,
  output F,
  output G
);

  wire and_1_out, and_2_out, and_3_out, and_4_out, and_5_out, and_6_out, and_7_out, and_8_out, and_9_out,
       and_10_out, not_1_out, not_2_out, not_3_out;

  not not_1 (not_1_out, in_1[2]);
  not not_2 (not_2_out, in_1[1]);
  not not_3 (not_3_out, in_1[0]);
  and and_1 (and_1_out, not_1_out, not_3_out);
  and and_2 (and_2_out, in_1[2], in_1[0]);
  and and_3 (and_3_out, not_1_out, in_1[1]);
  and and_4 (and_4_out, in_1[1], not_3_out);
  and and_5 (and_5_out, in_1[2], not_3_out);
  and and_6 (and_6_out, in_1[2], not_2_out);
  and and_7 (and_7_out, not_1_out, in_1[1]);
  and and_8 (and_8_out, not_2_out, not_3_out);
  and and_9 (and_9_out, in_1[0], in_1[1]);
  and and_10 (and_10_out, in_1[2], not_2_out, in_1[0]);
  or or_1 (A, and_1_out, in_1[1], and_2_out, in_1[3]);
  or or_2 (B, and_8_out, not_1_out, and_9_out);
  or or_3 (D, and_1_out, in_1[3], and_3_out, and_4_out, and_10_out);
  or or_4 (E, and_1_out, and_4_out);
  or or_5 (F, in_1[3], and_5_out, and_6_out, and_8_out);
  or or_6 (G, and_6_out, and_7_out, and_5_out, in_1[3]);
  or or_7 (C, not_2_out, in_1[0], in_1[2]);
endmodule
